// Logisim project compuertaFA.circ as structural Verilog: 1 circuit, main circuit FAGP
module FAGP (
  input  A,
  input  B,
  input  ci,
  output si,
  output pi,
  output gi
);

  wire xor_1_out;

  xor xor_1 (xor_1_out, A, B);
  or or_1 (pi, A, B);
  and and_1 (gi, A, B);
  xor xor_2 (si, xor_1_out, ci);
endmodule
